// Logisim project memory_controller.circ as structural Verilog: 1 circuit, main circuit main
module main (
);

  wire undriven_2, undriven_7, undriven_8;
  wire [1:0] undriven_3, undriven_4, undriven_5, undriven_6;
  wire [7:0] demultiplexer_1_out0, demultiplexer_1_out1, demultiplexer_1_out2, demultiplexer_1_out3,
       demultiplexer_2_out0, demultiplexer_2_out1, demultiplexer_2_out2, demultiplexer_2_out3,
       demultiplexer_3_out0, demultiplexer_3_out1, demultiplexer_3_out2, demultiplexer_3_out3,
       demultiplexer_4_out0, demultiplexer_4_out1, demultiplexer_4_out2, demultiplexer_4_out3,
       demultiplexer_5_out0, demultiplexer_5_out1, demultiplexer_5_out2, demultiplexer_5_out3,
       multiplexer_1_out, multiplexer_3_out, multiplexer_4_out, multiplexer_7_out, multiplexer_8_out,
       register_5_q, register_6_q, register_7_q, register_8_q, register_9_q, register_10_q, register_11_q,
       register_12_q, register_13_q, register_14_q, register_15_q, register_16_q, register_17_q,
       register_18_q, register_19_q, register_20_q, register_21_q, register_22_q, register_23_q,
       register_24_q, register_25_q, register_26_q, register_27_q, register_28_q, register_29_q,
       register_30_q, register_31_q, register_32_q, undriven;

  Demultiplexer #(.select(2), .width(8)) demultiplexer_1 (
    .out0(demultiplexer_1_out0), .out1(demultiplexer_1_out1), .out2(demultiplexer_1_out2),
    .out3(demultiplexer_1_out3), .in(undriven), .sel(undriven_3));
  Demultiplexer #(.select(2), .width(8)) demultiplexer_2 (
    .out0(demultiplexer_2_out0), .out1(demultiplexer_2_out1), .out2(demultiplexer_2_out2),
    .out3(demultiplexer_2_out3), .in(demultiplexer_1_out3), .sel(undriven_5));
  Register register_1 ();  // open: D, en, clk, Q, clr
  Register register_2 ();  // open: D, en, clk, Q, clr
  Register register_3 ();  // open: D, en, clk, Q, clr
  Register register_4 ();  // open: D, en, clk, Q, clr
  Register register_5 (.D(demultiplexer_2_out0), .en(undriven_2), .clk(undriven_7), .Q(register_5_q));  // open: clr
  Register register_6 (.D(demultiplexer_2_out1), .en(undriven_2), .clk(undriven_7), .Q(register_6_q));  // open: clr
  Register register_7 (.D(demultiplexer_2_out2), .en(undriven_2), .clk(undriven_7), .Q(register_7_q));  // open: clr
  Register register_8 (.D(demultiplexer_2_out3), .en(undriven_2), .clk(undriven_7), .Q(register_8_q));  // open: clr
  Register register_9 (.Q(register_9_q));  // open: D, en, clk, clr
  Register register_10 (.Q(register_10_q));  // open: D, en, clk, clr
  Register register_11 (.Q(register_11_q));  // open: D, en, clk, clr
  Register register_12 (.Q(register_12_q));  // open: D, en, clk, clr
  Demultiplexer #(.select(2), .width(8)) demultiplexer_3 (
    .out0(demultiplexer_3_out0), .out1(demultiplexer_3_out1), .out2(demultiplexer_3_out2),
    .out3(demultiplexer_3_out3), .in(demultiplexer_1_out2), .sel(undriven_5));
  Register register_13 (.D(demultiplexer_3_out0), .en(undriven_2), .clk(undriven_7), .Q(register_13_q));  // open: clr
  Register register_14 (.D(demultiplexer_3_out1), .en(undriven_2), .clk(undriven_7), .Q(register_14_q));  // open: clr
  Register register_15 (.D(demultiplexer_3_out2), .en(undriven_2), .clk(undriven_7), .Q(register_15_q));  // open: clr
  Register register_16 (.D(demultiplexer_3_out3), .en(undriven_2), .clk(undriven_7), .Q(register_16_q));  // open: clr
  Multiplexer #(.select(2), .width(8)) multiplexer_1 (
    .in0(register_5_q), .in1(register_6_q), .in2(register_7_q), .in3(register_8_q), .out(multiplexer_1_out),
    .sel(undriven_6));
  Register register_17 (.Q(register_17_q));  // open: D, en, clk, clr
  Register register_18 (.Q(register_18_q));  // open: D, en, clk, clr
  Register register_19 (.Q(register_19_q));  // open: D, en, clk, clr
  Register register_20 (.Q(register_20_q));  // open: D, en, clk, clr
  Multiplexer #(.select(2), .width(8)) multiplexer_2 (
    .in0(register_9_q), .in1(register_10_q), .in2(register_11_q), .in3(register_12_q));  // open: out, sel
  Demultiplexer #(.select(2), .width(8)) demultiplexer_4 (
    .out0(demultiplexer_4_out0), .out1(demultiplexer_4_out1), .out2(demultiplexer_4_out2),
    .out3(demultiplexer_4_out3), .in(demultiplexer_1_out1), .sel(undriven_5));
  Register register_21 (.D(demultiplexer_4_out0), .en(undriven_2), .clk(undriven_7), .Q(register_21_q));  // open: clr
  Register register_22 (.D(demultiplexer_4_out1), .en(undriven_2), .clk(undriven_7), .Q(register_22_q));  // open: clr
  Register register_23 (.D(demultiplexer_4_out2), .en(undriven_2), .clk(undriven_7), .Q(register_23_q));  // open: clr
  Register register_24 (.D(demultiplexer_4_out3), .en(undriven_2), .clk(undriven_7), .Q(register_24_q));  // open: clr
  Multiplexer #(.select(2), .width(8)) multiplexer_3 (
    .in0(register_13_q), .in1(register_14_q), .in2(register_15_q), .in3(register_16_q),
    .out(multiplexer_3_out), .sel(undriven_6));
  Register register_25 (.Q(register_25_q));  // open: D, en, clk, clr
  Register register_26 (.Q(register_26_q));  // open: D, en, clk, clr
  Register register_27 (.Q(register_27_q));  // open: D, en, clk, clr
  Register register_28 (.Q(register_28_q));  // open: D, en, clk, clr
  Demultiplexer #(.select(2), .width(8)) demultiplexer_5 (
    .out0(demultiplexer_5_out0), .out1(demultiplexer_5_out1), .out2(demultiplexer_5_out2),
    .out3(demultiplexer_5_out3), .in(demultiplexer_1_out0), .sel(undriven_5));
  Register register_29 (.D(demultiplexer_5_out0), .en(undriven_2), .clk(undriven_7), .Q(register_29_q));  // open: clr
  Register register_30 (.D(demultiplexer_5_out1), .en(undriven_2), .clk(undriven_7), .Q(register_30_q));  // open: clr
  Register register_31 (.D(demultiplexer_5_out2), .en(undriven_8), .clk(undriven_7), .Q(register_31_q));  // open: clr
  Register register_32 (.D(demultiplexer_5_out3), .en(undriven_2), .clk(undriven_7), .Q(register_32_q));  // open: clr
  Multiplexer #(.select(2), .width(8)) multiplexer_4 (
    .in0(register_21_q), .in1(register_22_q), .in2(register_23_q), .in3(register_24_q),
    .out(multiplexer_4_out), .sel(undriven_6));
  Multiplexer #(.select(2), .width(8)) multiplexer_5 (
    .in0(register_25_q), .in1(register_26_q), .in2(register_27_q), .in3(register_28_q));  // open: out, sel
  Multiplexer #(.select(2), .width(8)) multiplexer_6 (
    .in0(register_17_q), .in1(register_18_q), .in2(register_19_q), .in3(register_20_q));  // open: out, sel
  Multiplexer #(.select(2), .width(8)) multiplexer_7 (
    .in0(register_29_q), .in1(register_30_q), .in2(register_31_q), .in3(register_32_q),
    .out(multiplexer_7_out), .sel(undriven_6));
  Multiplexer #(.select(2), .width(8)) multiplexer_8 (
    .in0(multiplexer_7_out), .in1(multiplexer_4_out), .in2(multiplexer_3_out), .in3(multiplexer_1_out),
    .out(multiplexer_8_out), .sel(undriven_4));

  // Notes on the sheet:
  //   data_in
  //   address[0:1]
  //   address[2:3]
  //   wr_en
  //   clk
  //   address[0:1]
  //   address[2:3]
  //   data_out
endmodule
